// Logisim project CombinationalCircuits.circ as structural Verilog: 9 circuits, main circuit Half-Adder
module Half_Adder (
  input  x,
  input  y,
  output Sum,
  output Carry_Out
);

  and and_1 (Carry_Out, x, y);
  xor xor_1 (Sum, x, y);
endmodule

module Full_Adder (
  input  Carry_In,
  input  x,
  input  y,
  output Sum,
  output Carry_Out
);

  wire and_1_out, and_2_out, xor_1_out;

  and and_1 (and_1_out, x, y);
  xor xor_1 (xor_1_out, x, y);
  or or_1 (Carry_Out, and_1_out, and_2_out);
  and and_2 (and_2_out, Carry_In, xor_1_out);
  xor xor_2 (Sum, Carry_In, xor_1_out);
endmodule

module _8_bit_Ripple_Carry_Adder (
  input  in_1,
  input  in_2,
  input  in_3,
  input  in_4,
  input  in_5,
  input  in_6,
  input  in_7,
  input  in_8,
  input  in_9,
  input  in_10,
  input  in_11,
  input  in_12,
  input  in_13,
  input  in_14,
  input  in_15,
  input  in_16,
  output overflow,
  output out_18,
  output out_19,
  output out_20,
  output out_21,
  output out_22,
  output out_23,
  output out_24,
  output out_25,
  output out_26
);

  wire full_adder_1_carry_out, full_adder_3_carry_out, full_adder_4_carry_out, full_adder_5_carry_out,
       full_adder_6_carry_out, full_adder_7_carry_out, full_adder_8_carry_out;

  Full_Adder full_adder_1 (
    .x(in_2), .y(in_10), .Carry_In(full_adder_4_carry_out), .Carry_Out(full_adder_1_carry_out), .Sum(out_20));
  Full_Adder full_adder_2 (.x(in_1), .y(in_9), .Carry_In(full_adder_1_carry_out), .Carry_Out(out_18), .Sum(out_19));
  and and_1 (overflow, out_18, in_1, in_9);
  Full_Adder full_adder_3 (
    .x(in_4), .y(in_12), .Carry_In(full_adder_5_carry_out), .Carry_Out(full_adder_3_carry_out), .Sum(out_22));
  Full_Adder full_adder_4 (
    .x(in_3), .y(in_11), .Carry_In(full_adder_3_carry_out), .Carry_Out(full_adder_4_carry_out), .Sum(out_21));
  Full_Adder full_adder_5 (
    .x(in_5), .y(in_13), .Carry_In(full_adder_6_carry_out), .Carry_Out(full_adder_5_carry_out), .Sum(out_23));
  Full_Adder full_adder_6 (
    .x(in_6), .y(in_14), .Carry_In(full_adder_7_carry_out), .Carry_Out(full_adder_6_carry_out), .Sum(out_24));
  Full_Adder full_adder_7 (
    .x(in_7), .y(in_15), .Carry_In(full_adder_8_carry_out), .Carry_Out(full_adder_7_carry_out), .Sum(out_25));
  Full_Adder full_adder_8 (.x(in_8), .y(in_16), .Carry_In(1'b0), .Carry_Out(full_adder_8_carry_out), .Sum(out_26));

  // Other names for the same wires on the sheet: carry_out = out_18; s0 = out_26; s1 = out_25; s2 = out_24;
  //   s3 = out_23; s4 = out_22; s5 = out_21; s6 = out_20; s7 = out_19; x0 = in_8; x1 = in_7; x2 = in_6; x3 = in_5;
  //   x4 = in_4; x5 = in_3; x6 = in_2; x7 = in_1; y0 = in_16; y1 = in_15; y2 = in_14; y3 = in_13; y4 = in_12;
  //   y5 = in_11; y6 = in_10; y7 = in_9
endmodule

module _2_to_4_Decoder (
  input  x,
  input  y,
  input  in_3,
  input  in_4,
  input  in_5,
  input  in_6,
  input  [1:0] in_7,
  output xy,
  output xy_prime,
  output x_prime_y,
  output x_prime_y_prime
);

  wire not_1_out, not_2_out;

  not not_1 (not_1_out, x);
  not not_2 (not_2_out, y);
  Decoder #(.select(2)) decoder_1 (.out0(in_3), .out1(in_4), .out2(in_5), .out3(in_6), .sel(in_7), .en(1'b1));
  and and_1 (xy, x, y);
  and and_2 (xy_prime, x, not_2_out);
  and and_3 (x_prime_y, not_1_out, y);
  and and_4 (x_prime_y_prime, not_1_out, not_2_out);
endmodule

module Multiplexer (
  input  s1,
  input  s0,
  input  i3,
  input  i2,
  input  i1,
  input  i0,
  input  [3:0] in_7,
  input  [3:0] in_8,
  input  [3:0] in_9,
  input  [3:0] in_10,
  input  [1:0] in_11,
  output out_12
);

  wire and_1_out, and_2_out, and_3_out, and_4_out, not_1_out, not_2_out;
  wire [3:0] multiplexer_1_out;

  not not_1 (not_1_out, s1);
  not not_2 (not_2_out, s0);
  and and_1 (and_1_out, s1, s0, i3);
  and and_2 (and_2_out, s1, not_2_out, i2);
  and and_3 (and_3_out, not_1_out, s0, i1);
  and and_4 (and_4_out, not_1_out, not_2_out, i0);
  Hex_Digit_Display hex_digit_display_1 (.value(multiplexer_1_out));  // open: dp
  Multiplexer_part #(.select(2), .width(4)) multiplexer_1 (
    .in0(in_7), .in1(in_8), .in2(in_9), .in3(in_10), .out(multiplexer_1_out), .sel(in_11), .en(1'b1));
  or or_1 (out_12, and_1_out, and_2_out, and_3_out, and_4_out);
endmodule

module Demultiplexer (
  input  [3:0] in_1,
  input  [1:0] in_2
);

  wire [3:0] demultiplexer_1_out0, demultiplexer_1_out1, demultiplexer_1_out2, demultiplexer_1_out3;

  Demultiplexer_part #(.select(2), .width(4)) demultiplexer_1 (
    .out0(demultiplexer_1_out0), .out1(demultiplexer_1_out1), .out2(demultiplexer_1_out2),
    .out3(demultiplexer_1_out3), .in(in_1), .sel(in_2), .en(1'b1));
  Hex_Digit_Display hex_digit_display_1 (.value(demultiplexer_1_out0));  // open: dp
  Hex_Digit_Display hex_digit_display_2 (.value(demultiplexer_1_out1));  // open: dp
  Hex_Digit_Display hex_digit_display_3 (.value(demultiplexer_1_out2));  // open: dp
  Hex_Digit_Display hex_digit_display_4 (.value(demultiplexer_1_out3));  // open: dp
endmodule

module Bit_Selector (
  input  [31:0] in_1,
  input  [2:0] in_2
);

  wire [3:0] bitselector_1_out;

  BitSelector #(.width(32), .group(4)) bitselector_1 (.in(in_1), .out(bitselector_1_out), .sel(in_2));
  Hex_Digit_Display hex_digit_display_1 (.value(bitselector_1_out));  // open: dp
endmodule

module _4_bit_Shifter (
  input  i3,
  input  i2,
  input  i1,
  input  i0,
  input  s,
  output o3,
  output o2,
  output o1,
  output o0
);

  wire and_2_out, and_3_out, and_4_out, and_6_out, not_1_out;

  not not_1 (not_1_out, s);
  and and_1 (o3, not_1_out, i2);
  and and_2 (and_2_out, s, i3);
  and and_3 (and_3_out, i2, s);
  or or_1 (o2, and_2_out, and_4_out);
  and and_4 (and_4_out, not_1_out, i1);
  and and_5 (o0, i1, s);
  or or_2 (o1, and_3_out, and_6_out);
  and and_6 (and_6_out, not_1_out, i0);
endmodule

module _2_bit_ALU (
  input  b0,
  input  b1,
  input  a0,
  input  a1,
  input  f0,
  input  f1,
  output overflow,
  output c0,
  output c1
);

  wire and_1_out, and_2_out, and_3_out, and_4_out, and_5_out, and_6_out, and_7_out, and_8_out, and_9_out,
       and_10_out, and_11_out, and_12_out, and_13_out, and_14_out, and_15_out, and_16_out, and_17_out,
       not_1_out, not_2_out, not_3_out, not_4_out, not_5_out, not_6_out, or_2_out, or_4_out, xor_1_out,
       xor_2_out, xor_3_out;

  and and_1 (and_1_out, f1, f0);
  not not_1 (not_1_out, f0);
  and and_2 (and_2_out, not_1_out, f1);
  not not_2 (not_2_out, f1);
  buf and_3 (and_3_out, not_2_out);  // AND_Gate
  not not_3 (not_3_out, f0);
  and and_4 (and_4_out, not_3_out, not_4_out);
  not not_4 (not_4_out, f1);
  not not_5 (not_5_out, a0);
  and and_5 (and_5_out, b0, a0);
  and and_6 (and_6_out, and_5_out, and_1_out);
  and and_7 (and_7_out, not_5_out, and_2_out);
  or or_1 (c0, and_6_out, and_7_out, and_8_out, and_9_out);
  or or_2 (or_2_out, b0, a0);
  and and_8 (and_8_out, or_2_out, and_3_out);
  xor xor_1 (xor_1_out, b0, a0);
  and and_9 (and_9_out, xor_1_out, and_4_out);
  not not_6 (not_6_out, a1);
  and and_10 (and_10_out, b1, a1);
  and and_11 (and_11_out, and_10_out, and_1_out);
  and and_12 (and_12_out, b0, a0, and_4_out);
  or or_3 (c1, and_11_out, and_13_out, and_14_out, and_15_out);
  or or_4 (or_4_out, b1, a1);
  and and_13 (and_13_out, not_6_out, and_2_out);
  and and_14 (and_14_out, or_4_out, and_3_out);
  xor xor_2 (xor_2_out, b1, a1);
  xor xor_3 (xor_3_out, and_12_out, xor_2_out);
  and and_15 (and_15_out, xor_3_out, and_4_out);
  and and_16 (and_16_out, b1, a1, and_4_out);
  and and_17 (and_17_out, and_4_out, xor_2_out, and_12_out);
  or or_5 (overflow, and_16_out, and_17_out);

  // Notes on the sheet:
  //   decoder
  //   carry
  //   half-
  //   adder
  //   full-
  //   adder
endmodule
