// Logisim project Transistors.circ as structural Verilog
module intro (
  input  in_1,
  input  in_2,
  output out_3,
  output out_4
);

  Transistor transistor_1 ();  // open: in, out, gate
  Transistor #(.\type ("n")) transistor_2 (.in(1'b1), .out(out_3), .gate(in_1));
  Transistor #(.\type ("n")) transistor_3 (.in(1'b0), .out(out_4), .gate(in_2));

  // Notes on the sheet:
  //   gate
  //   source
  //   drain
endmodule

module NAND (
  input  a,
  input  b,
  output out_3
);

  wire transistor_3_out;

  Transistor transistor_1 (.in(1'b1), .out(out_3), .gate(b));
  Transistor transistor_2 (.in(1'b1), .out(out_3), .gate(a));
  Transistor #(.\type ("n")) transistor_3 (.in(1'b0), .out(transistor_3_out), .gate(a));
  Transistor #(.\type ("n")) transistor_4 (.in(transistor_3_out), .out(out_3), .gate(b));
endmodule

module NOR (
  input  a,
  input  b,
  output out_3
);

  wire transistor_2_out;

  Transistor #(.\type ("n")) transistor_1 (.in(1'b0), .out(out_3), .gate(a));
  Transistor transistor_2 (.in(1'b1), .out(transistor_2_out), .gate(b));
  Transistor transistor_3 (.in(transistor_2_out), .out(out_3), .gate(a));
  Transistor #(.\type ("n")) transistor_4 (.in(1'b0), .out(out_3), .gate(b));
endmodule
